// Digital circuit Template.dig as structural Verilog
module Template (
  input  X0,
  input  X1,
  input  S1,
  input  X2,
  input  X3,
  input  S0,
  output Z
);

  wire and_1_out, and_2_out, and_3_out, and_4_out, and_5_out, and_6_out, and_7_out, and_8_out, and_9_out,
       and_10_out, and_11_out, and_12_out, and_13_out, and_14_out, and_15_out, and_16_out, and_17_out,
       and_18_out, and_19_out, and_20_out, and_21_out, and_22_out, and_23_out, and_24_out, and_25_out,
       and_26_out, and_27_out, and_28_out, and_29_out, and_30_out, and_31_out, and_32_out, not_1_out,
       not_2_out, not_3_out, not_4_out, not_5_out, not_6_out, not_7_out, not_8_out, not_9_out, not_10_out,
       not_11_out, not_12_out, not_13_out, not_14_out, or_1_out, or_2_out, or_3_out, or_4_out;

  not not_1 (not_1_out, X1);
  not not_2 (not_2_out, X0);
  not not_3 (not_3_out, X0);
  not not_4 (not_4_out, X0);
  not not_5 (not_5_out, X2);
  not not_6 (not_6_out, X2);
  not not_7 (not_7_out, X1);
  not not_8 (not_8_out, X1);
  not not_9 (not_9_out, X3);
  not not_10 (not_10_out, X3);
  not not_11 (not_11_out, X3);
  not not_12 (not_12_out, X2);
  not not_13 (not_13_out, S1);
  not not_14 (not_14_out, S0);
  and and_1 (and_1_out, not_13_out, not_14_out, X0, not_1_out, not_5_out, not_9_out);
  and and_2 (and_2_out, not_13_out, not_14_out, X0, not_1_out, not_5_out, X3);
  and and_3 (and_3_out, not_13_out, not_14_out, X0, not_1_out, X2, not_9_out);
  and and_4 (and_4_out, not_13_out, not_14_out, X0, not_1_out, X2, X3);
  and and_5 (and_5_out, not_13_out, not_14_out, X0, X1, not_5_out, not_9_out);
  and and_6 (and_6_out, not_13_out, not_14_out, X0, X1, not_5_out, X3);
  and and_7 (and_7_out, not_13_out, not_14_out, X0, X1, X2, not_9_out);
  and and_8 (and_8_out, not_13_out, not_14_out, X0, X1, X2, X3);
  and and_9 (and_9_out, not_13_out, S0, X1, not_2_out, not_6_out, not_10_out);
  and and_10 (and_10_out, not_13_out, S0, X1, not_2_out, not_6_out, X3);
  and and_11 (and_11_out, not_13_out, S0, X1, not_2_out, X2, not_10_out);
  and and_12 (and_12_out, not_13_out, S0, X1, not_2_out, X2, X3);
  and and_13 (and_13_out, not_13_out, S0, X1, X0, not_6_out, not_10_out);
  and and_14 (and_14_out, not_13_out, S0, X1, X0, not_6_out, X3);
  and and_15 (and_15_out, not_13_out, S0, X1, X0, X2, not_10_out);
  and and_16 (and_16_out, not_13_out, S0, X1, X0, X2, X3);
  and and_17 (and_17_out, S1, not_14_out, X2, not_3_out, not_7_out, not_11_out);
  and and_18 (and_18_out, S1, not_14_out, X2, not_3_out, not_7_out, X3);
  and and_19 (and_19_out, S1, not_14_out, X2, not_3_out, X1, not_11_out);
  and and_20 (and_20_out, S1, not_14_out, X2, not_3_out, X1, X3);
  and and_21 (and_21_out, S1, not_14_out, X2, X0, not_7_out, not_11_out);
  and and_22 (and_22_out, S1, not_14_out, X2, X0, not_7_out, X3);
  and and_23 (and_23_out, S1, not_14_out, X2, X0, X1, not_11_out);
  and and_24 (and_24_out, S1, not_14_out, X2, X0, X1, X3);
  and and_25 (and_25_out, S1, S0, X3, not_4_out, not_8_out, not_12_out);
  and and_26 (and_26_out, S1, S0, X3, not_4_out, not_8_out, X2);
  and and_27 (and_27_out, S1, S0, X3, not_4_out, X1, not_12_out);
  and and_28 (and_28_out, S1, S0, X3, not_4_out, X1, X2);
  and and_29 (and_29_out, S1, S0, X3, X0, not_8_out, not_12_out);
  and and_30 (and_30_out, S1, S0, X3, X0, not_8_out, X2);
  and and_31 (and_31_out, S1, S0, X3, X0, X1, not_12_out);
  and and_32 (and_32_out, S1, S0, X3, X0, X1, X2);
  or or_1 (or_1_out, and_1_out, and_2_out, and_3_out, and_4_out, and_5_out, and_6_out, and_7_out, and_8_out);
  or or_2 (or_2_out, and_9_out, and_10_out, and_11_out, and_12_out, and_13_out, and_14_out, and_15_out, and_16_out);
  or or_3 (or_3_out, and_17_out, and_18_out, and_19_out, and_20_out, and_21_out, and_22_out, and_23_out, and_24_out);
  or or_4 (or_4_out, and_25_out, and_26_out, and_27_out, and_28_out, and_29_out, and_30_out, and_31_out, and_32_out);
  or or_5 (Z, or_1_out, or_2_out, or_3_out, or_4_out);
endmodule
