// Digital circuit B.dig as structural Verilog
module B (
  input  C1,
  input  C2,
  input  C3,
  output o1,
  output o2,
  output o3,
  output o4,
  output o5,
  output o6,
  output o7
);

  wire not_1_out, not_2_out, not_3_out;

  not not_1 (not_1_out, C1);
  not not_2 (not_2_out, C2);
  not not_3 (not_3_out, C3);
  and and_1 (o1, not_1_out, not_2_out, C3);
  and and_2 (o2, not_1_out, C2, not_3_out);
  and and_3 (o3, not_1_out, C2, C3);
  and and_4 (o4, C1, not_2_out, not_3_out);
  and and_5 (o5, C1, not_2_out, C3);
  and and_6 (o6, C1, C2, not_3_out);
  and and_7 (o7, C1, C2, C3);
endmodule
