// Digital circuit C.dig as structural Verilog
module C (
  input  m1,
  input  m2,
  input  m3,
  input  m4,
  input  p1,
  input  p2,
  input  p3,
  output C1,
  output C2,
  output C3
);

  wire xor_1_out, xor_2_out, xor_3_out, xor_4_out, xor_5_out, xor_6_out;

  xor xor_1 (xor_1_out, m2, p3);
  xor xor_2 (xor_2_out, m1, p2);
  xor xor_3 (xor_3_out, m1, p1);
  xor xor_4 (xor_4_out, xor_1_out, m3);
  xor xor_5 (xor_5_out, xor_2_out, m3);
  xor xor_6 (xor_6_out, xor_3_out, m2);
  xor xor_7 (C1, xor_4_out, m4);
  xor xor_8 (C2, xor_5_out, m4);
  xor xor_9 (C3, xor_6_out, m4);
endmodule
