// Digital circuit Template-03.dig as structural Verilog
module Template_03 (
  input  [3:0] In,
  input  [1:0] Selector,
  output [3:0] Output
);

  wire and_1_out, and_2_out, and_3_out, and_4_out, and_5_out, and_6_out, and_7_out, and_8_out, and_9_out,
       and_10_out, and_11_out, and_12_out, and_13_out, and_14_out, and_15_out, and_16_out, and_17_out,
       and_18_out, and_19_out, and_20_out, and_21_out, and_22_out, and_23_out, and_24_out, and_25_out,
       and_26_out, and_27_out, and_28_out, and_29_out, and_30_out, and_31_out, not_1_out, not_2_out,
       not_3_out, not_4_out, not_5_out, not_6_out;

  not not_1 (not_1_out, In[0]);
  not not_2 (not_2_out, In[1]);
  not not_3 (not_3_out, In[2]);
  not not_4 (not_4_out, In[3]);
  not not_5 (not_5_out, Selector[0]);
  not not_6 (not_6_out, Selector[1]);
  and and_1 (and_1_out, In[0], In[1], not_4_out, Selector[0], Selector[1]);
  and and_2 (and_2_out, In[0], not_2_out, In[2], not_4_out, Selector[1]);
  and and_3 (and_3_out, In[0], In[2], not_4_out, not_5_out);
  and and_4 (and_4_out, In[1], In[2], not_4_out, not_5_out);
  and and_5 (and_5_out, not_2_out, not_3_out, In[3]);
  and and_6 (and_6_out, In[0], not_2_out, not_3_out, not_5_out, not_6_out);
  and and_7 (and_7_out, In[0], not_2_out, not_3_out, Selector[0], Selector[1]);
  and and_8 (and_8_out, In[0], not_2_out, In[2], not_4_out, Selector[0], not_6_out);
  and and_9 (and_9_out, not_1_out, not_2_out, In[2], not_4_out, not_6_out);
  and and_10 (and_10_out, not_1_out, In[2], not_4_out, Selector[1]);
  and and_11 (and_11_out, not_2_out, not_3_out, In[3], Selector[0], not_6_out);
  and and_12 (and_12_out, not_2_out, not_3_out, In[3], not_5_out, Selector[1]);
  and and_13 (and_13_out, In[1], In[2], not_4_out, Selector[1]);
  and and_14 (and_14_out, In[1], not_3_out, not_4_out, not_5_out, not_6_out);
  and and_15 (and_15_out, In[1], In[2], not_4_out, Selector[0]);
  and and_16 (and_16_out, not_1_out, In[1], not_4_out, Selector[0], Selector[1]);
  and and_17 (and_17_out, In[0], In[1], not_4_out, not_5_out, not_6_out);
  and and_18 (and_18_out, not_1_out, not_2_out, not_3_out, not_5_out, not_6_out);
  and and_19 (and_19_out, In[0], not_2_out, In[2], not_4_out, Selector[0], not_6_out);
  and and_20 (and_20_out, not_1_out, not_2_out, In[2], not_4_out, not_6_out);
  and and_21 (and_21_out, In[0], not_2_out, In[2], not_4_out, Selector[1]);
  and and_22 (and_22_out, In[1], not_3_out, not_4_out, Selector[0], not_6_out);
  and and_23 (and_23_out, In[1], not_3_out, not_4_out, not_5_out, Selector[1]);
  and and_24 (and_24_out, not_2_out, not_3_out, In[3], Selector[1]);
  and and_25 (and_25_out, not_1_out, not_4_out, not_5_out, not_6_out);
  and and_26 (and_26_out, In[0], not_2_out, not_3_out, Selector[1]);
  and and_27 (and_27_out, not_1_out, not_2_out, not_3_out, not_5_out, not_6_out);
  and and_28 (and_28_out, In[0], not_2_out, In[2], not_4_out, Selector[0], not_6_out);
  and and_29 (and_29_out, not_1_out, In[1], not_4_out, not_6_out);
  and and_30 (and_30_out, In[0], not_2_out, not_3_out, Selector[0]);
  and and_31 (and_31_out, In[0], not_4_out, Selector[1]);
  or or_1 (Output[3], and_1_out, and_2_out, and_3_out, and_4_out, and_5_out);
  or or_2 (Output[2], and_6_out, and_7_out, and_8_out, and_9_out, and_10_out, and_11_out, and_12_out, and_13_out, and_14_out, and_15_out);
  or or_3 (Output[1], and_16_out, and_17_out, and_18_out, and_19_out, and_20_out, and_21_out, and_22_out, and_23_out, and_24_out);
  or or_4 (Output[0], and_25_out, and_26_out, and_27_out, and_28_out, and_29_out, and_30_out, and_31_out);

  // Other names for the same wires on the sheet: O0 = Output[0]; O1 = Output[1]; O2 = Output[2]; O3 = Output[3]
endmodule
