// Digital circuit Template-04.dig as structural Verilog
module Template_04 (
  input  [6:0] In,
  output [6:0] Output
);

  wire not_1_out, not_2_out, not_3_out, xor_1_out, xor_2_out, xor_3_out, xor_4_out, xor_5_out, xor_6_out,
       xor_7_out, xor_8_out, xor_9_out;
  wire [6:0] and_1_out;

  xor xor_1 (xor_1_out, In[2], In[3]);
  xor xor_2 (xor_2_out, In[4], In[5]);
  xor xor_3 (xor_3_out, In[4], In[6]);
  xor xor_4 (xor_4_out, xor_1_out, In[1]);
  xor xor_5 (xor_5_out, xor_2_out, In[1]);
  xor xor_6 (xor_6_out, xor_3_out, In[2]);
  xor xor_7 (xor_7_out, xor_4_out, In[0]);
  xor xor_8 (xor_8_out, xor_5_out, In[0]);
  xor xor_9 (xor_9_out, xor_6_out, In[0]);
  not not_1 (not_1_out, xor_7_out);
  not not_2 (not_2_out, xor_8_out);
  not not_3 (not_3_out, xor_9_out);
  and and_1 (and_1_out[6], not_1_out, not_2_out, xor_9_out);
  and and_2 (and_1_out[5], not_1_out, xor_8_out, not_3_out);
  and and_3 (and_1_out[4], not_1_out, xor_8_out, xor_9_out);
  and and_4 (and_1_out[3], xor_7_out, not_2_out, not_3_out);
  and and_5 (and_1_out[2], xor_7_out, not_2_out, xor_9_out);
  and and_6 (and_1_out[1], xor_7_out, xor_8_out, not_3_out);
  and and_7 (and_1_out[0], xor_7_out, xor_8_out, xor_9_out);
  assign Output = In ^ and_1_out;  // XOr xor_10, 7 bits wide
endmodule
