// Digital circuit Template.dig as structural Verilog
module Template (
  input  [3:0] A,
  input  [3:0] B,
  input  [2:0] S,
  input  M,
  input  C,
  output [3:0] F,
  output [3:0] Cout
);

  wire [3:0] add_1_s, add_2_s, add_3_s, add_4_s, add_5_s, add_6_s, barrelshifter_1_out, barrelshifter_2_out,
       Logic_3_out, multiplexer_1_out, not_1_out, not_2_out;

  assign not_1_out = ~B;  // Not not_1, 4 bits wide
  assign not_2_out = ~A;  // Not not_2, 4 bits wide
  LookUpTable Logic (.in0(B[0]), .in1(A[0]), .in2(S[0]), .in3(S[1]), .in4(S[2]), .out(Logic_3_out[0]));
  LookUpTable Logic_2 (.in0(B[1]), .in1(A[1]), .in2(S[0]), .in3(S[1]), .in4(S[2]), .out(Logic_3_out[1]));
  LookUpTable Logic_3 (.in0(B[2]), .in1(A[2]), .in2(S[0]), .in3(S[1]), .in4(S[2]), .out(Logic_3_out[2]));
  LookUpTable Logic_4 (.in0(B[3]), .in1(A[3]), .in2(S[0]), .in3(S[1]), .in4(S[2]), .out(Logic_3_out[3]));
  Add #(.Bits(4)) add_1 (.a(A), .b(4'b0000), .c_i(C), .s(add_1_s));  // open: c_o
  Add #(.Bits(4)) add_2 (.a(A), .b(4'b1111), .c_i(C), .s(add_2_s));  // open: c_o
  Add #(.Bits(4)) add_3 (.a(A), .b(B), .c_i(C), .s(add_3_s));  // open: c_o
  Add #(.Bits(4)) add_4 (.a(A), .b(not_1_out), .c_i(C), .s(add_4_s));  // open: c_o
  Add #(.Bits(4)) add_5 (.a(not_2_out), .b(4'b0000), .c_i(C), .s(add_5_s));  // open: c_o
  Add #(.Bits(4)) add_6 (.a(4'b0000), .b(B), .c_i(C), .s(add_6_s));  // open: c_o
  BarrelShifter #(.Bits(4)) barrelshifter_1 (.in(A), .shift(3'b001), .out(barrelshifter_1_out));
  BarrelShifter #(.Bits(4), .direction("right")) barrelshifter_2 (.in(A), .shift(3'b001), .out(barrelshifter_2_out));
  Multiplexer #(.Bits(4), .Selector_Bits(3)) multiplexer_1 (
    .sel(S), .in_0(add_1_s), .in_1(add_2_s), .in_2(add_3_s), .in_3(add_4_s), .in_4(add_5_s), .in_5(add_6_s),
    .in_6(barrelshifter_1_out), .in_7(barrelshifter_2_out), .out(multiplexer_1_out));
  Multiplexer #(.Bits(4)) multiplexer_2 (.sel(M), .in_0(Logic_3_out), .in_1(multiplexer_1_out), .out(F));
  LookUpTable lookuptable_1 ();  // open: in0, in1, in2, in3, in4, out

  assign Cout = 4'b0000;

  // Notes on the sheet:
  //   contents of Logic (hex, n*v repeats v):
  //   1,1,0,0,1,1,1,0,1,0,0,0,1,0,0,1,0,0,0,1,0,1,1,1,0,0,1,0,0,0,1,1
  //   contents of Logic_2 (hex, n*v repeats v):
  //   1,1,0,0,1,1,1,0,1,0,0,0,1,0,0,1,0,0,0,1,0,1,1,1,0,0,1,0,0,0,1,1
  //   contents of Logic_3 (hex, n*v repeats v):
  //   1,1,0,0,1,1,1,0,1,0,0,0,1,0,0,1,0,0,0,1,0,1,1,1,0,0,1,0,0,0,1,1
  //   contents of Logic_4 (hex, n*v repeats v):
  //   1,1,0,0,1,1,1,0,1,0,0,0,1,0,0,1,0,0,0,1,0,1,1,1,0,0,1,0,0,0,1,1
endmodule
