// Digital circuit Template.dig as structural Verilog
module Template (
  input  J,
  input  K,
  input  Clear,
  input  Clock,
  output Q,
  output Q_2
);

  wire and_1_out, and_2_out, and_3_out, and_4_out, and_5_out, not_1_out, not_2_out, not_3_out, or_1_out,
       rs_ff_as_1_nq, rs_ff_as_1_q, rs_ff_as_2_nq, rs_ff_as_2_q;

  and and_1 (and_1_out, Q, K, Clock);
  and and_2 (and_2_out, Clock, J, Q_2);
  RS_FF_AS rs_ff_as_1 (.S(and_2_out), .R(and_1_out), .Q(rs_ff_as_1_q), .nQ(rs_ff_as_1_nq));
  not not_1 (not_1_out, Clock);
  or or_1 (or_1_out, Clear, rs_ff_as_1_nq);
  and and_3 (and_3_out, rs_ff_as_1_q, not_2_out);
  not not_2 (not_2_out, Clear);
  and and_4 (and_4_out, not_1_out, or_1_out);
  and and_5 (and_5_out, and_3_out, not_1_out);
  RS_FF_AS rs_ff_as_2 (.S(and_5_out), .R(and_4_out), .Q(rs_ff_as_2_q), .nQ(rs_ff_as_2_nq));
  not not_3 (not_3_out, Clear);
  or or_2 (Q_2, Clear, rs_ff_as_2_nq);
  and and_6 (Q, rs_ff_as_2_q, not_3_out);
endmodule
