// Digital circuit Template.dig as structural Verilog
module Template (
  input  T,
  input  Clear,
  input  Clock,
  output Q,
  output Q_2
);

  wire and_1_out, and_2_out, and_3_out, and_4_out, and_5_out, nor_1_out, nor_2_out, not_1_out, or_1_out;

  not not_1 (not_1_out, Clock);
  and and_1 (and_1_out, Q, T, not_1_out);
  and and_2 (and_2_out, not_1_out, T, Q_2);
  or or_1 (or_1_out, Clear, and_1_out);
  and and_3 (and_3_out, and_2_out, ~Clear);  // And
  nor nor_1 (nor_1_out, nor_2_out, or_1_out);
  nor nor_2 (nor_2_out, nor_1_out, and_3_out);
  and and_4 (and_4_out, Clock, nor_1_out);
  and and_5 (and_5_out, nor_2_out, Clock);
  nor nor_3 (Q_2, Q, and_4_out);
  nor nor_4 (Q, Q_2, and_5_out);
endmodule
