// Digital circuit Template.dig as structural Verilog
module Template (
  input  P,
  input  T,
  input  A,
  input  Clr,
  input  Load,
  input  Clock,
  input  B,
  input  C,
  input  D,
  output QA,
  output RCO,
  output QB,
  output QC,
  output QD
);

  wire and_1_out, and_3_out, and_4_out, and_5_out, multiplexer_1_out, multiplexer_2_out, multiplexer_3_out,
       multiplexer_4_out, multiplexer_5_out, multiplexer_6_out, multiplexer_7_out, multiplexer_8_out,
       multiplexer_9_out, multiplexer_10_out, multiplexer_11_out, multiplexer_12_out, PT, xor_1_out,
       xor_2_out, xor_3_out, xor_4_out;

  xor xor_1 (xor_1_out, and_1_out, QA);
  and and_1 (and_1_out, 1'b1, 1'b1, 1'b1);
  and and_2 (PT, P, T);
  Multiplexer multiplexer_1 (.sel(PT), .in_0(QA), .in_1(xor_1_out), .out(multiplexer_1_out));
  Multiplexer multiplexer_2 (.sel(Clr), .in_0(1'b0), .in_1(multiplexer_1_out), .out(multiplexer_2_out));
  Multiplexer multiplexer_3 (.sel(Load), .in_0(A), .in_1(multiplexer_2_out), .out(multiplexer_3_out));
  D_FF d_ff_1 (.D(multiplexer_3_out), .C(Clock), .Q(QA));  // open: nQ
  and and_3 (and_3_out, 1'b1, 1'b1, QA);
  xor xor_2 (xor_2_out, and_3_out, QB);
  Multiplexer multiplexer_4 (.sel(PT), .in_0(QB), .in_1(xor_2_out), .out(multiplexer_4_out));
  Multiplexer multiplexer_5 (.sel(Clr), .in_0(1'b0), .in_1(multiplexer_4_out), .out(multiplexer_5_out));
  Multiplexer multiplexer_6 (.sel(Load), .in_0(B), .in_1(multiplexer_5_out), .out(multiplexer_6_out));
  D_FF d_ff_2 (.D(multiplexer_6_out), .C(Clock), .Q(QB));  // open: nQ
  xor xor_3 (xor_3_out, and_4_out, QC);
  and and_4 (and_4_out, 1'b1, QB, QA);
  Multiplexer multiplexer_7 (.sel(PT), .in_0(QC), .in_1(xor_3_out), .out(multiplexer_7_out));
  Multiplexer multiplexer_8 (.sel(Clr), .in_0(1'b0), .in_1(multiplexer_7_out), .out(multiplexer_8_out));
  Multiplexer multiplexer_9 (.sel(Load), .in_0(C), .in_1(multiplexer_8_out), .out(multiplexer_9_out));
  D_FF d_ff_3 (.D(multiplexer_9_out), .C(Clock), .Q(QC));  // open: nQ
  xor xor_4 (xor_4_out, and_5_out, QD);
  and and_5 (and_5_out, QC, QB, QA);
  Multiplexer multiplexer_10 (.sel(PT), .in_0(QD), .in_1(xor_4_out), .out(multiplexer_10_out));
  Multiplexer multiplexer_11 (.sel(Clr), .in_0(1'b0), .in_1(multiplexer_10_out), .out(multiplexer_11_out));
  Multiplexer multiplexer_12 (.sel(Load), .in_0(D), .in_1(multiplexer_11_out), .out(multiplexer_12_out));
  D_FF d_ff_4 (.D(multiplexer_12_out), .C(Clock), .Q(QD));  // open: nQ
  and and_6 (RCO, QD, QC, QB, QA);
endmodule

/* Test case:
P T D C B A \Clr \Load Clock QD QC QB QA RCO
0 0 x x x x 0 1 0 x x x x x
0 0 x x x x 0 1 1 0 0 0 0 0
loop(a,15)
	x x bits(4,a) 0 0 0 x x x x 0
	x x bits(4,a) 0 0 1 bits(4,a) 0
end loop
*/
