// Digital circuit Template.dig as structural Verilog
module Template (
  input  P,
  input  Clr,
  input  clock,
  output Z
);

  wire and_1_out, and_2_out, d_ff_1_q, not_1_out;

  and and_1 (and_1_out, ~Clr, P);  // And
  D_FF d_ff_1 (.D(and_1_out), .C(clock), .Q(d_ff_1_q));  // open: nQ
  not not_1 (not_1_out, d_ff_1_q);
  and and_2 (and_2_out, P, not_1_out);
  D_FF d_ff_2 (.D(and_2_out), .C(clock), .Q(Z));  // open: nQ
endmodule
