// Digital circuit Parist.dig as structural Verilog
module Parist (
  input  clock,
  input  P5,
  input  P10,
  input  P20,
  input  Pcoffee,
  input  Ptea,
  input  reset,
  input  Pchange,
  input  Pnext,
  output CoffeeOut,
  output TeaOut,
  output [5:0] Balance,
  output [1:0] Change20,
  output [1:0] Change10,
  output [1:0] Change5
);

  wire add_1_c_o, and_1_out, and_2_out, and_3_out, and_4_out, and_5_out, and_6_out, and_7_out, and_13_out,
       and_14_out, coffee_do, coffee_ok, coffee_op, comparator_1_gt, comparator_2_eq, comparator_2_gt,
       comparator_3_eq, comparator_3_gt, d_ff_1_q, d_ff_2_q, d_ff_3_q, d_ff_5_q, d_ff_6_q, d_ff_7_q,
       d_ff_8_q, d_ff_20_q, d_ff_21_q, gt__eq_20, gt__eq_25, lt__eq_50, nor_1_out, not_1_out, not_2_out,
       not_3_out, not_4_out, not_5_out, not_6_out, not_7_out, not_8_out, not_9_out, operating, or_2_out,
       or_3_out, or_5_out, p5_t, p10_t, p20_t, pchange_t, pcoffee_t, pnext_t, ptea_t, tea_do, tea_ok, tea_op;
  wire [1:0] multiplexer_4_out, multiplexer_5_out, multiplexer_6_out, multiplexer_7_out, multiplexer_8_out,
       multiplexer_9_out;
  wire [2:0] and_10_out;
  wire [5:0] add_1_s, balance___20, balance___25, c5, c10, c20, d_ff_15_q, div_1_r, div_2_r,
       multiplexer_1_out, multiplexer_2_out, multiplexer_3_out, multiplexer_10_out, multiplexer_11_out;

  not not_1 (not_1_out, d_ff_1_q);
  not not_2 (not_2_out, d_ff_2_q);
  not not_3 (not_3_out, d_ff_3_q);
  not not_4 (not_4_out, d_ff_5_q);
  not not_5 (not_5_out, d_ff_6_q);
  not not_6 (not_6_out, d_ff_7_q);
  not not_7 (not_7_out, d_ff_8_q);
  and and_1 (and_1_out, P5, not_1_out);
  and and_2 (and_2_out, P10, not_2_out);
  and and_3 (and_3_out, P20, not_3_out);
  and and_4 (and_4_out, Pcoffee, not_4_out);
  and and_5 (and_5_out, Ptea, not_5_out);
  and and_6 (and_6_out, Pchange, not_6_out);
  and and_7 (and_7_out, Pnext, not_7_out);
  D_FF d_ff_1 (.D(P5), .C(clock), .Q(d_ff_1_q));  // open: nQ
  D_FF d_ff_2 (.D(P10), .C(clock), .Q(d_ff_2_q));  // open: nQ
  D_FF d_ff_3 (.D(P20), .C(clock), .Q(d_ff_3_q));  // open: nQ
  D_FF d_ff_4 (.D(and_3_out), .C(clock), .Q(p20_t));  // open: nQ
  D_FF d_ff_5 (.D(Pcoffee), .C(clock), .Q(d_ff_5_q));  // open: nQ
  D_FF d_ff_6 (.D(Ptea), .C(clock), .Q(d_ff_6_q));  // open: nQ
  D_FF d_ff_7 (.D(Pchange), .C(clock), .Q(d_ff_7_q));  // open: nQ
  D_FF d_ff_8 (.D(Pnext), .C(clock), .Q(d_ff_8_q));  // open: nQ
  D_FF d_ff_9 (.D(and_1_out), .C(clock), .Q(p5_t));  // open: nQ
  D_FF d_ff_10 (.D(and_2_out), .C(clock), .Q(p10_t));  // open: nQ
  D_FF d_ff_11 (.D(and_4_out), .C(clock), .Q(pcoffee_t));  // open: nQ
  D_FF d_ff_12 (.D(and_5_out), .C(clock), .Q(ptea_t));  // open: nQ
  D_FF d_ff_13 (.D(and_6_out), .C(clock), .Q(pchange_t));  // open: nQ
  D_FF d_ff_14 (.D(and_7_out), .C(clock), .Q(pnext_t));  // open: nQ
  Multiplexer #(.Selector_Bits(2), .Bits(6)) multiplexer_1 (
    .sel({tea_ok, coffee_ok}), .in_0(Balance), .in_1(balance___25), .in_2(balance___20), .in_3({6{1'b0}}),
    .out(multiplexer_1_out));
  D_FF #(.Bits(6)) d_ff_15 (.D(multiplexer_2_out), .C(clock), .Q(d_ff_15_q));  // open: nQ
  and and_8 (and_10_out[0], p5_t, ~operating);  // And
  and and_9 (and_10_out[1], p10_t, ~operating);  // And
  and and_10 (and_10_out[2], p20_t, ~operating);  // And
  or or_1 (operating, CoffeeOut, coffee_op, tea_op, TeaOut);
  Multiplexer #(.Bits(6)) multiplexer_2 (.sel(pchange_t), .in_0(Balance), .in_1(d_ff_15_q), .out(multiplexer_2_out));
  Multiplexer #(.Selector_Bits(3), .Bits(6)) multiplexer_3 (
    .sel(and_10_out), .in_0({6{1'b0}}), .in_1(6'b000101), .in_2(6'b001010), .in_3({6{1'b0}}),
    .in_4(6'b010100), .in_5({6{1'b0}}), .in_6({6{1'b0}}), .in_7({6{1'b0}}), .out(multiplexer_3_out));
  Div #(.Bits(6)) div_1 (.a(multiplexer_2_out), .b(6'b010100), .q(c20), .r(div_1_r));
  Add #(.Bits(6)) add_1 (.a(multiplexer_1_out), .b(multiplexer_3_out), .c_i(1'b0), .s(add_1_s), .c_o(add_1_c_o));
  Sub #(.Bits(6)) sub_1 (.a(Balance), .b(6'b011001), .c_i(1'b0), .s(balance___25));  // open: c_o
  and and_11 (coffee_do, gt__eq_25, ~operating, pcoffee_t);  // And
  nor nor_1 (nor_1_out, pchange_t, pnext_t, reset);
  and and_12 (tea_do, gt__eq_20, ~operating, ptea_t);  // And
  Div #(.Bits(6)) div_2 (.a(div_1_r), .b(6'b001010), .q(c10), .r(div_2_r));
  Div #(.Bits(6)) div_3 (.a(div_2_r), .b(6'b000101), .q(c5));  // open: r
  Comparator #(.Bits(6)) comparator_1 (.a(add_1_s), .b(6'b110010), .gt(comparator_1_gt));  // open: eq, lt
  D_FF d_ff_16 (.D(coffee_do), .C(clock), .Q(coffee_op));  // open: nQ
  or or_2 (or_2_out, coffee_op, CoffeeOut);
  or or_3 (or_3_out, tea_op, TeaOut);
  D_FF d_ff_17 (.D(tea_do), .C(clock), .Q(tea_op));  // open: nQ
  nor nor_2 (lt__eq_50, comparator_1_gt, add_1_c_o);
  Sub #(.Bits(6)) sub_2 (.a(Balance), .b(6'b010100), .c_i(1'b0), .s(balance___20));  // open: c_o
  Comparator #(.Bits(6)) comparator_2 (
    .a(Balance), .b(6'b011001), .gt(comparator_2_gt), .eq(comparator_2_eq));  // open: lt
  and and_13 (and_13_out, or_2_out, nor_1_out);
  and and_14 (and_14_out, nor_1_out, or_3_out);
  not not_8 (not_8_out, d_ff_20_q);
  not not_9 (not_9_out, d_ff_21_q);
  Multiplexer #(.Bits(2)) multiplexer_4 (.sel(pchange_t), .in_0(Change20), .in_1(c20[1:0]), .out(multiplexer_4_out));
  Multiplexer #(.Bits(2)) multiplexer_5 (.sel(pchange_t), .in_0(Change10), .in_1(c10[1:0]), .out(multiplexer_5_out));
  Multiplexer #(.Bits(2)) multiplexer_6 (.sel(pchange_t), .in_0(Change5), .in_1(c5[1:0]), .out(multiplexer_6_out));
  and and_15 (coffee_ok, coffee_do, not_8_out);
  and and_16 (tea_ok, tea_do, not_9_out);
  Multiplexer #(.Bits(2)) multiplexer_7 (.sel(reset), .in_0(multiplexer_4_out), .in_1(2'b00), .out(multiplexer_7_out));
  Multiplexer #(.Bits(2)) multiplexer_8 (.sel(reset), .in_0(multiplexer_5_out), .in_1(2'b00), .out(multiplexer_8_out));
  Multiplexer #(.Bits(2)) multiplexer_9 (.sel(reset), .in_0(multiplexer_6_out), .in_1(2'b00), .out(multiplexer_9_out));
  Multiplexer #(.Bits(6)) multiplexer_10 (.sel(lt__eq_50), .in_0(Balance), .in_1(add_1_s), .out(multiplexer_10_out));
  or or_4 (gt__eq_25, comparator_2_gt, comparator_2_eq);
  D_FF d_ff_18 (.D(and_14_out), .C(clock), .Q(TeaOut));  // open: nQ
  or or_5 (or_5_out, reset, pchange_t);
  D_FF d_ff_19 (.D(and_13_out), .C(clock), .Q(CoffeeOut));  // open: nQ
  D_FF d_ff_20 (.D(coffee_do), .C(clock), .Q(d_ff_20_q));  // open: nQ
  D_FF d_ff_21 (.D(tea_do), .C(clock), .Q(d_ff_21_q));  // open: nQ
  Multiplexer #(.Bits(6)) multiplexer_11 (
    .sel(or_5_out), .in_0(multiplexer_10_out), .in_1({6{1'b0}}), .out(multiplexer_11_out));
  D_FF #(.Bits(2)) d_ff_22 (.D(multiplexer_7_out), .C(clock), .Q(Change20));  // open: nQ
  D_FF #(.Bits(2)) d_ff_23 (.D(multiplexer_8_out), .C(clock), .Q(Change10));  // open: nQ
  D_FF #(.Bits(2)) d_ff_24 (.D(multiplexer_9_out), .C(clock), .Q(Change5));  // open: nQ
  D_FF #(.Bits(6)) d_ff_25 (.D(multiplexer_11_out), .C(clock), .Q(Balance));  // open: nQ
  Comparator #(.Bits(6)) comparator_3 (
    .a(Balance), .b(6'b010100), .gt(comparator_3_gt), .eq(comparator_3_eq));  // open: lt
  or or_6 (gt__eq_20, comparator_3_gt, comparator_3_eq);

  // Other names for the same wires on the sheet: cout = CoffeeOut; tout = TeaOut
endmodule
