// Digital circuit Template.dig as structural Verilog
module Template (
  input  P5,
  input  reset,
  input  clock,
  input  P10,
  input  P20,
  input  Pcoffee,
  input  Ptea,
  input  Pchange,
  input  Pnext,
  output [5:0] Balance,
  output CoffeeOut,
  output TeaOut,
  output [1:0] Change5,
  output [1:0] Change10,
  output [1:0] Change20
);

  wire a0000, a0001, a0010, a0011, a0100, a0101, a0110, a0111, a1000, a1001, a1010, a1011, a1100, a1101,
       a1110, a1111, and_1_out, and_2_out, and_3_out, and_4_out, and_5_out, and_6_out, and_7_out, and_11_out,
       and_12_out, and_13_out, and_14_out, and_15_out, and_17_out, and_18_out, and_19_out, and_20_out,
       and_21_out, and_22_out, and_23_out, and_26_out, and_27_out, and_28_out, and_29_out, and_30_out,
       and_31_out, and_32_out, and_33_out, and_34_out, and_35_out, and_36_out, and_37_out, and_38_out,
       and_39_out, balance5, balance10, balance20, balance25, balance30, balance40, balance45,
       balance__geq_5_eq, balance__geq_5_gt, balance__geq_10_eq, balance__geq_10_gt, balance__geq_20_eq,
       balance__geq_20_gt, balance__geq_25_eq, balance__geq_25_gt, balance__leq_30_eq, balance__leq_30_lt,
       balance__leq_40_eq, balance__leq_40_lt, balance__leq_45_eq, balance__leq_45_lt, d_ff_1_q, d_ff_2_q,
       d_ff_3_q, d_ff_7_q, d_ff_8_q, d_ff_9_q, d_ff_10_q, multiplexer_3_out, multiplexer_4_out,
       multiplexer_9_out, multiplexer_10_out, multiplexer_15_out, multiplexer_16_out, multiplexer_17_out,
       multiplexer_21_out, multiplexer_23_out, multiplexer_24_out, not_1_out, not_2_out, not_3_out,
       not_4_out, not_5_out, not_6_out, not_7_out, not_8_out, not_9_out, not_10_out, not_11_out, not_12_out,
       not_13_out, not_14_out, not_15_out, not_17_out, not_18_out, not_19_out, not_20_out, not_21_out,
       not_23_out, not_24_out, not_25_out, not_26_out, not_27_out, not_28_out, not_29_out, or_8_out,
       or_9_out, or_10_out, or_11_out, or_12_out, or_13_out, out00001, out00111, out01000, out01001,
       out01010, out01100, out10001, out10111, out11000, out11001, out11010, out20001, out20111, out21000,
       out21100, out30001, out30111, out31000, out31001, out31010, p5_t, p10_t, p20_t, pchange_t, pcoffee_t,
       pnext_t, ptea_t;
  wire [1:0] change5plus1, change10plus1, change20plus1, multiplexer_5_out, multiplexer_6_out,
       multiplexer_7_out, multiplexer_11_out, multiplexer_12_out, multiplexer_13_out;
  wire [3:0] allq;
  wire [5:0] balanceminus5, balanceminus10, balanceminus20, balanceminus25, balanceplus5, balanceplus10,
       balanceplus20, multiplexer_1_out, multiplexer_2_out, multiplexer_8_out, multiplexer_14_out,
       multiplexer_18_out, multiplexer_19_out, multiplexer_20_out, multiplexer_22_out;

  Sub #(.Bits(6)) balance___eq__5 (.a(Balance), .b(6'b000101), .c_i(1'b0), .s(balanceminus5));  // open: c_o
  Sub #(.Bits(6)) balance___eq__10 (.a(Balance), .b(6'b001010), .c_i(1'b0), .s(balanceminus10));  // open: c_o
  Sub #(.Bits(6)) balance___eq__20 (.a(Balance), .b(6'b010100), .c_i(1'b0), .s(balanceminus20));  // open: c_o
  Sub #(.Bits(6)) balance___eq__25 (.a(Balance), .b(6'b011001), .c_i(1'b0), .s(balanceminus25));  // open: c_o
  Add #(.Bits(6)) balance__plus__eq__5 (.a(Balance), .b(6'b000101), .c_i(1'b0), .s(balanceplus5));  // open: c_o
  Add #(.Bits(6)) balance__plus__eq__10 (.a(Balance), .b(6'b001010), .c_i(1'b0), .s(balanceplus10));  // open: c_o
  Add #(.Bits(6)) balance__plus__eq__20 (.a(Balance), .b(6'b010100), .c_i(1'b0), .s(balanceplus20));  // open: c_o
  Comparator #(.Bits(6)) balance__leq_30 (
    .a(Balance), .b(6'b011110), .eq(balance__leq_30_eq), .lt(balance__leq_30_lt));  // open: gt
  Comparator #(.Bits(6)) balance__leq_40 (
    .a(Balance), .b(6'b101000), .eq(balance__leq_40_eq), .lt(balance__leq_40_lt));  // open: gt
  Comparator #(.Bits(6)) balance__leq_45 (
    .a(Balance), .b(6'b101101), .eq(balance__leq_45_eq), .lt(balance__leq_45_lt));  // open: gt
  Comparator #(.Bits(6)) balance__geq_25 (
    .a(Balance), .b(6'b011001), .gt(balance__geq_25_gt), .eq(balance__geq_25_eq));  // open: lt
  Comparator #(.Bits(6)) balance__geq_20 (
    .a(Balance), .b(6'b010100), .gt(balance__geq_20_gt), .eq(balance__geq_20_eq));  // open: lt
  Comparator #(.Bits(6)) balance__geq_10 (
    .a(Balance), .b(6'b001010), .gt(balance__geq_10_gt), .eq(balance__geq_10_eq));  // open: lt
  Comparator #(.Bits(6)) balance__geq_5 (
    .a(Balance), .b(6'b000101), .gt(balance__geq_5_gt), .eq(balance__geq_5_eq));  // open: lt
  Add #(.Bits(2)) change20_plus__plus (.a(Change20), .b(2'b01), .c_i(1'b0), .s(change20plus1));  // open: c_o
  Add #(.Bits(2)) change10_plus__plus (.a(Change10), .b(2'b01), .c_i(1'b0), .s(change10plus1));  // open: c_o
  Add #(.Bits(2)) change5_plus__plus (.a(Change5), .b(2'b01), .c_i(1'b0), .s(change5plus1));  // open: c_o
  or or_1 (balance30, balance__leq_30_eq, balance__leq_30_lt);
  or or_2 (balance40, balance__leq_40_eq, balance__leq_40_lt);
  or or_3 (balance45, balance__leq_45_eq, balance__leq_45_lt);
  or or_4 (balance25, balance__geq_25_gt, balance__geq_25_eq);
  or or_5 (balance20, balance__geq_20_gt, balance__geq_20_eq);
  or or_6 (balance10, balance__geq_10_gt, balance__geq_10_eq);
  or or_7 (balance5, balance__geq_5_gt, balance__geq_5_eq);
  D_FF d_ff_1 (.D(P5), .C(clock), .Q(d_ff_1_q));  // open: nQ
  D_FF d_ff_2 (.D(P10), .C(clock), .Q(d_ff_2_q));  // open: nQ
  D_FF d_ff_3 (.D(P20), .C(clock), .Q(d_ff_3_q));  // open: nQ
  not not_1 (not_1_out, d_ff_1_q);
  not not_2 (not_2_out, d_ff_2_q);
  not not_3 (not_3_out, d_ff_3_q);
  and and_1 (and_1_out, P5, not_1_out);
  and and_2 (and_2_out, P10, not_2_out);
  and and_3 (and_3_out, P20, not_3_out);
  D_FF d_ff_4 (.D(and_1_out), .C(clock), .Q(p5_t));  // open: nQ
  D_FF d_ff_5 (.D(and_2_out), .C(clock), .Q(p10_t));  // open: nQ
  D_FF d_ff_6 (.D(and_3_out), .C(clock), .Q(p20_t));  // open: nQ
  Multiplexer #(.Bits(6)) multiplexer_1 (.sel(a0100), .in_0(Balance), .in_1(balanceplus5), .out(multiplexer_1_out));
  Multiplexer #(.Bits(6)) multiplexer_2 (
    .sel(a0011), .in_0(multiplexer_1_out), .in_1(balanceplus10), .out(multiplexer_2_out));
  Demultiplexer #(.Selector_Bits(4)) demultiplexer_1 (
    .sel(allq), .in(1'b1), .out_0(a0000), .out_1(a0001), .out_2(a0010), .out_3(a0011), .out_4(a0100),
    .out_5(a0101), .out_6(a0110), .out_7(a0111), .out_8(a1000), .out_9(a1001), .out_10(a1010),
    .out_11(a1011), .out_12(a1100), .out_13(a1101), .out_14(a1110), .out_15(a1111));
  Multiplexer multiplexer_3 (.sel(a0110), .in_0(TeaOut), .in_1(1'b1), .out(multiplexer_3_out));
  Multiplexer multiplexer_4 (.sel(a0101), .in_0(CoffeeOut), .in_1(1'b1), .out(multiplexer_4_out));
  Multiplexer #(.Bits(2)) multiplexer_5 (.sel(a1001), .in_0(Change20), .in_1(change20plus1), .out(multiplexer_5_out));
  Multiplexer #(.Bits(2)) multiplexer_6 (.sel(a1010), .in_0(Change10), .in_1(change10plus1), .out(multiplexer_6_out));
  Multiplexer #(.Bits(2)) multiplexer_7 (.sel(a1011), .in_0(Change5), .in_1(change5plus1), .out(multiplexer_7_out));
  Multiplexer #(.Bits(6)) multiplexer_8 (
    .sel(a0010), .in_0(multiplexer_2_out), .in_1(balanceplus20), .out(multiplexer_8_out));
  Multiplexer multiplexer_9 (.sel(or_8_out), .in_0(multiplexer_3_out), .in_1(1'b0), .out(multiplexer_9_out));
  or or_8 (or_8_out, a0000, a0001);
  Multiplexer multiplexer_10 (.sel(or_9_out), .in_0(multiplexer_4_out), .in_1(1'b0), .out(multiplexer_10_out));
  or or_9 (or_9_out, a0000, a0001);
  Multiplexer #(.Bits(2)) multiplexer_11 (
    .sel(or_10_out), .in_0(multiplexer_5_out), .in_1(2'b00), .out(multiplexer_11_out));
  or or_10 (or_10_out, a0000, a1000);
  Multiplexer #(.Bits(2)) multiplexer_12 (
    .sel(or_11_out), .in_0(multiplexer_6_out), .in_1(2'b00), .out(multiplexer_12_out));
  or or_11 (or_11_out, a0000, a1000);
  Multiplexer #(.Bits(2)) multiplexer_13 (
    .sel(or_12_out), .in_0(multiplexer_7_out), .in_1(2'b00), .out(multiplexer_13_out));
  or or_12 (or_12_out, a0000, a1000);
  D_FF d_ff_7 (.D(Pcoffee), .C(clock), .Q(d_ff_7_q));  // open: nQ
  D_FF d_ff_8 (.D(Ptea), .C(clock), .Q(d_ff_8_q));  // open: nQ
  D_FF d_ff_9 (.D(Pchange), .C(clock), .Q(d_ff_9_q));  // open: nQ
  D_FF d_ff_10 (.D(Pnext), .C(clock), .Q(d_ff_10_q));  // open: nQ
  Multiplexer #(.Bits(6)) multiplexer_14 (
    .sel(a0101), .in_0(multiplexer_8_out), .in_1(balanceminus25), .out(multiplexer_14_out));
  not not_4 (not_4_out, d_ff_7_q);
  not not_5 (not_5_out, d_ff_8_q);
  not not_6 (not_6_out, d_ff_9_q);
  not not_7 (not_7_out, d_ff_10_q);
  Multiplexer multiplexer_15 (.sel(a1000), .in_0(multiplexer_9_out), .in_1(1'b0), .out(multiplexer_15_out));
  Multiplexer multiplexer_16 (.sel(a1000), .in_0(multiplexer_10_out), .in_1(1'b0), .out(multiplexer_16_out));
  D_FF #(.Bits(2)) d_ff_11 (.D(multiplexer_11_out), .C(clock), .Q(Change20));  // open: nQ
  D_FF #(.Bits(2)) d_ff_12 (.D(multiplexer_12_out), .C(clock), .Q(Change10));  // open: nQ
  D_FF #(.Bits(2)) d_ff_13 (.D(multiplexer_13_out), .C(clock), .Q(Change5));  // open: nQ
  and and_4 (and_4_out, Pcoffee, not_4_out);
  and and_5 (and_5_out, Ptea, not_5_out);
  and and_6 (and_6_out, Pchange, not_6_out);
  and and_7 (and_7_out, Pnext, not_7_out);
  Multiplexer #(.Selector_Bits(4)) multiplexer_17 (
    .sel(allq), .in_0(1'b0), .in_1(out30001), .in_2(1'b0), .in_3(1'b0), .in_4(1'b0), .in_5(1'b0),
    .in_6(1'b0), .in_7(out30111), .in_8(out31000), .in_9(1'b1), .in_10(1'b1), .in_11(1'b1), .in_12(out31001),
    .in_13(out31010), .in_14(1'b0), .in_15(1'b0), .out(multiplexer_17_out));
  Multiplexer #(.Bits(6)) multiplexer_18 (
    .sel(or_13_out), .in_0(multiplexer_14_out), .in_1(balanceminus20), .out(multiplexer_18_out));
  or or_13 (or_13_out, a0110, a1001);
  D_FF d_ff_14 (.D(and_4_out), .C(clock), .Q(pcoffee_t));  // open: nQ
  D_FF d_ff_15 (.D(and_5_out), .C(clock), .Q(ptea_t));  // open: nQ
  D_FF d_ff_16 (.D(and_6_out), .C(clock), .Q(pchange_t));  // open: nQ
  D_FF d_ff_17 (.D(and_7_out), .C(clock), .Q(pnext_t));  // open: nQ
  D_FF d_ff_18 (.D(multiplexer_17_out), .C(clock), .Q(allq[3]));  // open: nQ
  Multiplexer #(.Bits(6)) multiplexer_19 (
    .sel(a1010), .in_0(multiplexer_18_out), .in_1(balanceminus10), .out(multiplexer_19_out));
  D_FF d_ff_19 (.D(multiplexer_15_out), .C(clock), .Q(TeaOut));  // open: nQ
  D_FF d_ff_20 (.D(multiplexer_16_out), .C(clock), .Q(CoffeeOut));  // open: nQ
  Multiplexer #(.Bits(6)) multiplexer_20 (
    .sel(a1011), .in_0(multiplexer_19_out), .in_1(balanceminus5), .out(multiplexer_20_out));
  Multiplexer #(.Selector_Bits(4)) multiplexer_21 (
    .sel(allq), .in_0(1'b0), .in_1(out20001), .in_2(1'b0), .in_3(1'b0), .in_4(1'b0), .in_5(1'b1),
    .in_6(1'b1), .in_7(out20111), .in_8(out21000), .in_9(1'b1), .in_10(1'b1), .in_11(1'b1), .in_12(1'b0),
    .in_13(1'b0), .in_14(1'b0), .in_15(1'b0), .out(multiplexer_21_out));
  Multiplexer #(.Bits(6)) multiplexer_22 (
    .sel(a0000), .in_0(multiplexer_20_out), .in_1({6{1'b0}}), .out(multiplexer_22_out));
  D_FF d_ff_21 (.D(multiplexer_21_out), .C(clock), .Q(allq[2]));  // open: nQ
  D_FF #(.Bits(6)) d_ff_22 (.D(multiplexer_22_out), .C(clock), .Q(Balance));  // open: nQ
  Multiplexer #(.Selector_Bits(4)) multiplexer_23 (
    .sel(allq), .in_0(1'b0), .in_1(out10001), .in_2(1'b0), .in_3(1'b0), .in_4(1'b0), .in_5(1'b1),
    .in_6(1'b1), .in_7(out10111), .in_8(out11000), .in_9(1'b0), .in_10(1'b0), .in_11(1'b1), .in_12(out11001),
    .in_13(out11010), .in_14(1'b0), .in_15(1'b0), .out(multiplexer_23_out));
  D_FF d_ff_23 (.D(multiplexer_23_out), .C(clock), .Q(allq[1]));  // open: nQ
  Multiplexer #(.Selector_Bits(4)) multiplexer_24 (
    .sel(allq), .in_0(1'b1), .in_1(out00001), .in_2(1'b1), .in_3(1'b1), .in_4(1'b1), .in_5(1'b1),
    .in_6(1'b1), .in_7(out00111), .in_8(out01000), .in_9(1'b0), .in_10(1'b1), .in_11(1'b0), .in_12(out01001),
    .in_13(out01010), .in_14(1'b1), .in_15(1'b1), .out(multiplexer_24_out));
  D_FF d_ff_24 (.D(multiplexer_24_out), .C(clock), .Q(allq[0]));  // open: nQ
  not not_8 (not_8_out, pchange_t);
  not not_9 (not_9_out, pnext_t);
  not not_10 (not_10_out, balance10);
  not not_11 (not_11_out, balance20);
  not not_12 (not_12_out, balance10);
  not not_13 (not_13_out, balance20);
  not not_14 (not_14_out, reset);
  not not_15 (not_15_out, balance5);
  and and_8 (out30111, pchange_t, not_14_out);
  and and_9 (out20111, not_8_out, not_9_out, not_14_out);
  and and_10 (out10111, not_8_out, not_9_out, not_14_out);
  and and_11 (and_11_out, not_8_out, not_9_out, not_14_out);
  and and_12 (and_12_out, pnext_t, not_14_out);
  and and_13 (and_13_out, not_10_out, not_11_out, balance5);
  and and_14 (and_14_out, not_10_out, not_11_out, not_15_out);
  and and_15 (and_15_out, balance10, not_11_out);
  and and_16 (out21000, not_10_out, not_11_out, not_15_out);
  and and_17 (and_17_out, not_10_out, not_11_out, balance5);
  and and_18 (and_18_out, balance10, not_11_out);
  and and_19 (and_19_out, not_10_out, not_11_out, balance5);
  and and_20 (and_20_out, balance10, not_13_out);
  and and_21 (and_21_out, not_13_out, balance5);
  and and_22 (and_22_out, balance10, not_13_out);
  and and_23 (and_23_out, not_13_out, balance5);
  or or_14 (out01001, not_12_out, balance20);
  or or_15 (out00111, and_11_out, and_12_out);
  or or_16 (out31000, and_13_out, and_14_out, and_15_out, balance20);
  or or_17 (out11000, and_17_out, and_18_out);
  or or_18 (out01000, and_19_out, balance20);
  or or_19 (out31001, and_20_out, and_21_out, balance20);
  or or_20 (out11001, and_22_out, and_23_out);
  not not_16 (out01010, balance10);
  not not_17 (not_17_out, balance20);
  or or_21 (out31010, balance10, balance5);
  or or_22 (out11010, balance10, balance5);
  not not_18 (not_18_out, balance30);
  not not_19 (not_19_out, balance45);
  not not_20 (not_20_out, CoffeeOut);
  not not_21 (not_21_out, p10_t);
  not not_22 (out21100, reset);
  not not_23 (not_23_out, p20_t);
  not not_24 (not_24_out, p5_t);
  and and_24 (out01100, pchange_t, out21100);
  not not_25 (not_25_out, pchange_t);
  not not_26 (not_26_out, pcoffee_t);
  not not_27 (not_27_out, ptea_t);
  not not_28 (not_28_out, reset);
  not not_29 (not_29_out, TeaOut);
  and and_25 (out30001, not_21_out, not_23_out, not_24_out, pchange_t, not_26_out, not_27_out, not_28_out);
  and and_26 (and_26_out, balance20, not_20_out, not_21_out, not_23_out, not_24_out, not_26_out, ptea_t, not_28_out, not_29_out);
  and and_27 (and_27_out, balance25, not_20_out, not_21_out, not_23_out, not_24_out, pcoffee_t, not_28_out, not_29_out);
  and and_28 (and_28_out, balance45, not_21_out, not_23_out, p5_t, not_28_out);
  and and_29 (and_29_out, balance20, not_20_out, not_21_out, not_23_out, not_24_out, not_26_out, ptea_t, not_28_out, not_29_out);
  and and_30 (and_30_out, balance30, p20_t, not_28_out);
  and and_31 (and_31_out, balance40, p10_t, not_23_out, not_28_out);
  and and_32 (and_32_out, not_17_out, not_23_out, not_24_out, ptea_t, not_28_out);
  and and_33 (and_33_out, not_18_out, p20_t, not_28_out);
  and and_34 (and_34_out, not_19_out, not_23_out, p5_t, not_28_out);
  and and_35 (and_35_out, CoffeeOut, not_23_out, not_24_out, ptea_t, not_28_out);
  and and_36 (and_36_out, p10_t, not_23_out, not_28_out);
  and and_37 (and_37_out, not_23_out, not_24_out, not_25_out, not_27_out, not_28_out);
  and and_38 (and_38_out, not_23_out, not_24_out, ptea_t, not_28_out, TeaOut);
  and and_39 (and_39_out, not_23_out, not_24_out, pcoffee_t, not_28_out);
  or or_23 (out20001, and_26_out, and_27_out, and_28_out);
  or or_24 (out10001, and_29_out, and_30_out, and_31_out);
  or or_25 (out00001, and_32_out, and_33_out, and_34_out, and_35_out, and_36_out, and_37_out, and_38_out, and_39_out);

  // Other names for the same wires on the sheet: clk = clock; out31100 = out21100; q0 = allq[0]; q1 = allq[1];
  //   q2 = allq[2]; q3 = allq[3]; rst = reset

  // Notes on the sheet:
  //   0111
  //   1000
  //   1100
  //   1101
  //   0001
endmodule

/* Test case:
clock reset P5 P10 P20 Pcoffee Ptea Pchange Pnext Balance CoffeeOut TeaOut Change5 Change10 Change20
0 1 0 0 0 0 0 0 0 x x x x x x
1 1 0 0 0 0 0 0 0 0 0 0 0 0 0
0 0 1 0 0 0 0 0 0 0 0 0 0 0 0
1 0 1 0 0 0 0 0 0 0 0 0 0 0 0
0 0 0 0 0 0 0 0 0 x x x x x x
1 0 0 0 0 0 0 0 0 x x x x x x
0 0 0 0 0 0 0 0 0 x x x x x x
1 0 0 0 0 0 0 0 0 x x x x x x
0 0 0 0 0 0 0 0 0 x x x x x x
1 0 0 0 0 0 0 0 0 x x x x x x
0 0 0 0 0 0 0 0 0 x x x x x x
1 0 0 0 0 0 0 0 0 x x x x x x
0 0 0 0 0 0 0 0 0 x x x x x x
1 0 0 0 0 0 0 0 0 x x x x x x
0 0 0 0 0 0 0 0 0 x x x x x x
1 0 0 0 0 0 0 0 0 x x x x x x
0 0 0 0 0 0 0 0 0 x x x x x x
1 0 0 0 0 0 0 0 0 x x x x x x
0 0 0 0 0 0 0 0 0 x x x x x x
1 0 0 0 0 0 0 0 0 x x x x x x
0 0 0 0 0 0 0 0 0 x x x x x x
1 0 0 0 0 0 0 0 0 x x x x x x
0 0 0 0 0 0 0 0 0 x x x x x x
1 0 0 0 0 0 0 0 0 x x x x x x
0 0 0 0 0 0 0 0 0 x x x x x x
1 0 0 0 0 0 0 0 0 x x x x x x
0 0 0 0 0 0 0 0 0 x x x x x x
1 0 0 0 0 0 0 0 0 x x x x x x
0 0 0 0 0 0 0 0 0 x x x x x x
1 0 0 0 0 0 0 0 0 x x x x x x
0 0 0 0 0 0 0 0 0 x x x x x x
1 0 0 0 0 0 0 0 0 x x x x x x
0 0 0 0 0 0 0 0 0 x x x x x x
1 0 0 0 0 0 0 0 0 x x x x x x
0 0 0 0 0 0 0 0 0 x x x x x x
1 0 0 0 0 0 0 0 0 x x x x x x
0 0 0 0 0 0 0 0 0 x x x x x x
1 0 0 0 0 0 0 0 0 x x x x x x
0 0 0 0 0 0 0 0 0 x x x x x x
1 0 0 0 0 0 0 0 0 x x x x x x
0 0 0 0 0 0 0 0 0 x x x x x x
1 0 0 0 0 0 0 0 0 x x x x x x
0 0 0 0 0 0 0 0 0 x x x x x x
1 0 0 0 0 0 0 0 0 x x x x x x
0 0 0 0 0 0 0 0 0 5 0 0 0 0 0
1 0 0 0 0 0 0 0 0 5 0 0 0 0 0
0 0 0 1 0 0 0 0 0 5 0 0 0 0 0
1 0 0 1 0 0 0 0 0 5 0 0 0 0 0
0 0 0 0 0 0 0 0 0 x x x x x x
1 0 0 0 0 0 0 0 0 x x x x x x
0 0 0 0 0 0 0 0 0 x x x x x x
1 0 0 0 0 0 0 0 0 x x x x x x
*/

/* Test case:
clock reset P5 P10 P20 Pcoffee Ptea Pchange Pnext Balance CoffeeOut TeaOut Change5 Change10 Change20
0 1 0 0 0 0 0 0 0 x x x x x x
1 1 0 0 0 0 0 0 0 0 0 0 0 0 0
0 0 0 0 0 1 0 0 0 0 0 0 0 0 0
1 0 0 0 0 1 0 0 0 0 0 0 0 0 0
0 0 0 0 0 0 0 0 0 x x x x x x
1 0 0 0 0 0 0 0 0 x x x x x x
0 0 0 0 0 0 0 0 0 x x x x x x
1 0 0 0 0 0 0 0 0 x x x x x x
0 0 0 0 0 0 0 0 0 x x x x x x
1 0 0 0 0 0 0 0 0 x x x x x x
0 0 0 0 0 0 0 0 0 x x x x x x
1 0 0 0 0 0 0 0 0 x x x x x x
0 0 0 0 0 0 0 0 0 x x x x x x
1 0 0 0 0 0 0 0 0 x x x x x x
0 0 0 0 0 0 0 0 0 x x x x x x
1 0 0 0 0 0 0 0 0 x x x x x x
0 0 0 0 0 0 0 0 0 x x x x x x
1 0 0 0 0 0 0 0 0 x x x x x x
0 0 0 0 0 0 0 0 0 x x x x x x
1 0 0 0 0 0 0 0 0 x x x x x x
0 0 0 0 0 0 0 0 0 x x x x x x
1 0 0 0 0 0 0 0 0 x x x x x x
0 0 0 0 0 0 0 0 0 x x x x x x
1 0 0 0 0 0 0 0 0 x x x x x x
0 0 0 0 0 0 0 0 0 x x x x x x
1 0 0 0 0 0 0 0 0 x x x x x x
0 0 0 0 0 0 0 0 0 x x x x x x
1 0 0 0 0 0 0 0 0 x x x x x x
0 0 0 0 0 0 0 0 0 x x x x x x
1 0 0 0 0 0 0 0 0 x x x x x x
0 0 0 0 0 0 0 0 0 x x x x x x
1 0 0 0 0 0 0 0 0 x x x x x x
0 0 0 0 0 0 0 0 0 x x x x x x
1 0 0 0 0 0 0 0 0 x x x x x x
0 0 0 0 0 0 0 0 0 x x x x x x
1 0 0 0 0 0 0 0 0 x x x x x x
0 0 0 0 0 0 0 0 0 x x x x x x
1 0 0 0 0 0 0 0 0 x x x x x x
0 0 0 0 0 0 0 0 0 x x x x x x
1 0 0 0 0 0 0 0 0 x x x x x x
0 0 0 0 0 0 0 0 0 x x x x x x
1 0 0 0 0 0 0 0 0 x x x x x x
0 0 0 0 0 0 0 0 0 x x x x x x
1 0 0 0 0 0 0 0 0 x x x x x x
0 0 0 0 0 0 0 0 0 0 0 0 0 0 0
1 0 0 0 0 0 0 0 0 0 0 0 0 0 0
0 0 0 0 0 0 1 0 0 0 0 0 0 0 0
1 0 0 0 0 0 1 0 0 0 0 0 0 0 0
0 0 0 0 0 0 0 0 0 x x x x x x
1 0 0 0 0 0 0 0 0 x x x x x x
0 0 0 0 0 0 0 0 0 x x x x x x
1 0 0 0 0 0 0 0 0 x x x x x x
*/

/* Test case:
clock reset P5 P10 P20 Pcoffee Ptea Pchange Pnext Balance CoffeeOut TeaOut Change5 Change10 Change20
0 1 0 0 0 0 0 0 0 x x x x x x
1 1 0 0 0 0 0 0 0 0 0 0 0 0 0
0 0 1 0 0 0 0 0 0 0 0 0 0 0 0
1 0 1 0 0 0 0 0 0 0 0 0 0 0 0
0 0 0 0 0 0 0 0 0 x x x x x x
1 0 0 0 0 0 0 0 0 x x x x x x
0 0 0 0 0 0 0 0 0 x x x x x x
1 0 0 0 0 0 0 0 0 x x x x x x
0 0 0 0 0 0 0 0 0 x x x x x x
1 0 0 0 0 0 0 0 0 x x x x x x
0 0 0 0 0 0 0 0 0 x x x x x x
1 0 0 0 0 0 0 0 0 x x x x x x
0 0 0 0 0 0 0 0 0 x x x x x x
1 0 0 0 0 0 0 0 0 x x x x x x
0 0 0 0 0 0 0 0 0 x x x x x x
1 0 0 0 0 0 0 0 0 x x x x x x
0 0 0 0 0 0 0 0 0 x x x x x x
1 0 0 0 0 0 0 0 0 x x x x x x
0 0 0 0 0 0 0 0 0 x x x x x x
1 0 0 0 0 0 0 0 0 x x x x x x
0 0 0 0 0 0 0 0 0 x x x x x x
1 0 0 0 0 0 0 0 0 x x x x x x
0 0 0 0 0 0 0 0 0 x x x x x x
1 0 0 0 0 0 0 0 0 x x x x x x
0 0 0 0 0 0 0 0 0 x x x x x x
1 0 0 0 0 0 0 0 0 x x x x x x
0 0 0 0 0 0 0 0 0 x x x x x x
1 0 0 0 0 0 0 0 0 x x x x x x
0 0 0 0 0 0 0 0 0 x x x x x x
1 0 0 0 0 0 0 0 0 x x x x x x
0 0 0 0 0 0 0 0 0 x x x x x x
1 0 0 0 0 0 0 0 0 x x x x x x
0 0 0 0 0 0 0 0 0 x x x x x x
1 0 0 0 0 0 0 0 0 x x x x x x
0 0 0 0 0 0 0 0 0 x x x x x x
1 0 0 0 0 0 0 0 0 x x x x x x
0 0 0 0 0 0 0 0 0 x x x x x x
1 0 0 0 0 0 0 0 0 x x x x x x
0 0 0 0 0 0 0 0 0 x x x x x x
1 0 0 0 0 0 0 0 0 x x x x x x
0 0 0 0 0 0 0 0 0 x x x x x x
1 0 0 0 0 0 0 0 0 x x x x x x
0 0 0 0 0 0 0 0 0 x x x x x x
1 0 0 0 0 0 0 0 0 x x x x x x
0 0 0 0 0 0 0 0 0 5 0 0 0 0 0
1 0 0 0 0 0 0 0 0 5 0 0 0 0 0
0 0 0 0 0 0 0 1 0 5 0 0 0 0 0
1 0 0 0 0 0 0 1 0 5 0 0 0 0 0
0 0 0 0 0 0 0 0 0 x x x x x x
1 0 0 0 0 0 0 0 0 x x x x x x
0 0 0 0 0 0 0 0 0 x x x x x x
1 0 0 0 0 0 0 0 0 x x x x x x
*/

/* Test case:
clock reset P5 P10 P20 Pcoffee Ptea Pchange Pnext Balance CoffeeOut TeaOut Change5 Change10 Change20
0 1 0 0 0 0 0 0 0 x x x x x x
1 1 0 0 0 0 0 0 0 0 0 0 0 0 0
0 0 0 0 1 0 0 0 0 0 0 0 0 0 0
1 0 0 0 1 0 0 0 0 0 0 0 0 0 0
0 0 0 0 0 0 0 0 0 x x x x x x
1 0 0 0 0 0 0 0 0 x x x x x x
0 0 0 0 0 0 0 0 0 x x x x x x
1 0 0 0 0 0 0 0 0 x x x x x x
0 0 0 0 0 0 0 0 0 x x x x x x
1 0 0 0 0 0 0 0 0 x x x x x x
0 0 0 0 0 0 0 0 0 x x x x x x
1 0 0 0 0 0 0 0 0 x x x x x x
0 0 0 0 0 0 0 0 0 x x x x x x
1 0 0 0 0 0 0 0 0 x x x x x x
0 0 0 0 0 0 0 0 0 x x x x x x
1 0 0 0 0 0 0 0 0 x x x x x x
0 0 0 0 0 0 0 0 0 x x x x x x
1 0 0 0 0 0 0 0 0 x x x x x x
0 0 0 0 0 0 0 0 0 x x x x x x
1 0 0 0 0 0 0 0 0 x x x x x x
0 0 0 0 0 0 0 0 0 x x x x x x
1 0 0 0 0 0 0 0 0 x x x x x x
0 0 0 0 0 0 0 0 0 x x x x x x
1 0 0 0 0 0 0 0 0 x x x x x x
0 0 0 0 0 0 0 0 0 x x x x x x
1 0 0 0 0 0 0 0 0 x x x x x x
0 0 0 0 0 0 0 0 0 x x x x x x
1 0 0 0 0 0 0 0 0 x x x x x x
0 0 0 0 0 0 0 0 0 x x x x x x
1 0 0 0 0 0 0 0 0 x x x x x x
0 0 0 0 0 0 0 0 0 x x x x x x
1 0 0 0 0 0 0 0 0 x x x x x x
0 0 0 0 0 0 0 0 0 x x x x x x
1 0 0 0 0 0 0 0 0 x x x x x x
0 0 0 0 0 0 0 0 0 x x x x x x
1 0 0 0 0 0 0 0 0 x x x x x x
0 0 0 0 0 0 0 0 0 x x x x x x
1 0 0 0 0 0 0 0 0 x x x x x x
0 0 0 0 0 0 0 0 0 x x x x x x
1 0 0 0 0 0 0 0 0 x x x x x x
0 0 0 0 0 0 0 0 0 x x x x x x
1 0 0 0 0 0 0 0 0 x x x x x x
0 0 0 0 0 0 0 0 0 x x x x x x
1 0 0 0 0 0 0 0 0 x x x x x x
0 0 0 0 0 0 0 0 0 20 0 0 0 0 0
1 0 0 0 0 0 0 0 0 20 0 0 0 0 0
0 0 0 0 1 0 0 0 0 20 0 0 0 0 0
1 0 0 0 1 0 0 0 0 20 0 0 0 0 0
0 0 0 0 0 0 0 0 0 x x x x x x
1 0 0 0 0 0 0 0 0 x x x x x x
0 0 0 0 0 0 0 0 0 x x x x x x
1 0 0 0 0 0 0 0 0 x x x x x x
*/
