// Digital circuit quiz2.dig as structural Verilog
module quiz2 (
  input  [7:0] in0,
  input  [7:0] in1,
  input  addsubtract,
  output [4:0] out
);

  wire add_1_c_o, add_1_s, add_2_c_o, add_2_s, add_3_c_o, add_3_s, add_4_c_o, add_4_s, add_5_c_o, add_5_s,
       add_6_c_o, add_6_s, add_7_c_o, add_8_c_o, add_8_s, add_9_c_o, add_10_c_o, add_10_s, add_11_c_o,
       add_12_c_o, add_13_c_o;
  wire [3:0] m0, m1, multiplexer_1_out, not_1_out;

  assign not_1_out = ~m1;  // Not not_1, 4 bits wide
  Add add_1 (.a(in0[0]), .b(in0[1]), .c_i(in0[2]), .s(add_1_s), .c_o(add_1_c_o));
  Add add_2 (.a(in0[3]), .b(in0[4]), .c_i(in0[5]), .s(add_2_s), .c_o(add_2_c_o));
  Add add_3 (.a(in0[6]), .b(in0[7]), .c_i(1'b0), .s(add_3_s), .c_o(add_3_c_o));
  Add add_4 (.a(in1[0]), .b(in1[1]), .c_i(in1[2]), .s(add_4_s), .c_o(add_4_c_o));
  Add add_5 (.a(in1[3]), .b(in1[4]), .c_i(in1[5]), .s(add_5_s), .c_o(add_5_c_o));
  Add add_6 (.a(in1[6]), .b(in1[7]), .c_i(1'b0), .s(add_6_s), .c_o(add_6_c_o));
  Multiplexer #(.Bits(4)) multiplexer_1 (.sel(addsubtract), .in_0(m1), .in_1(not_1_out), .out(multiplexer_1_out));
  Add add_7 (.a(add_1_s), .b(add_2_s), .c_i(add_3_s), .s(m0[0]), .c_o(add_7_c_o));
  Add add_8 (.a(add_1_c_o), .b(add_2_c_o), .c_i(add_3_c_o), .s(add_8_s), .c_o(add_8_c_o));
  Add add_9 (.a(add_4_s), .b(add_5_s), .c_i(add_6_s), .s(m1[0]), .c_o(add_9_c_o));
  Add add_10 (.a(add_4_c_o), .b(add_5_c_o), .c_i(add_6_c_o), .s(add_10_s), .c_o(add_10_c_o));
  Add #(.Bits(4)) add_11 (.a(m0), .b(multiplexer_1_out), .c_i(addsubtract), .s(out[3:0]), .c_o(add_11_c_o));
  Multiplexer multiplexer_2 (.sel(addsubtract), .in_0(add_11_c_o), .in_1(1'b0), .out(out[4]));
  Add add_12 (.a(add_7_c_o), .b(add_8_s), .c_i(1'b0), .s(m0[1]), .c_o(add_12_c_o));
  Add add_13 (.a(add_9_c_o), .b(add_10_s), .c_i(1'b0), .s(m1[1]), .c_o(add_13_c_o));
  Add add_14 (.a(add_12_c_o), .b(add_8_c_o), .c_i(1'b0), .s(m0[2]), .c_o(m0[3]));
  Add add_15 (.a(add_13_c_o), .b(add_10_c_o), .c_i(1'b0), .s(m1[2]), .c_o(m1[3]));
endmodule
