// Digital circuit quiz25.dig as structural Verilog
module quiz25 (
  input  [7:0] in,
  output [3:0] out
);

  wire and_1_out, and_2_out, and_3_out, and_4_out, and_5_out, and_6_out, and_7_out, and_8_out, and_9_out,
       and_10_out, and_11_out, and_12_out, and_13_out, and_14_out, and_15_out, and_16_out, and_17_out,
       and_18_out, not_1_out, not_2_out, not_3_out, not_4_out, not_5_out, not_6_out, not_7_out, not_8_out,
       not_9_out, not_10_out, not_11_out;
  wire [2:0] or_3_out, or_4_out;

  not not_1 (not_1_out, in[0]);
  not not_2 (not_2_out, in[1]);
  not not_3 (not_3_out, in[2]);
  not not_4 (not_4_out, in[2]);
  not not_5 (not_5_out, in[4]);
  not not_6 (not_6_out, in[3]);
  not not_7 (not_7_out, in[4]);
  not not_8 (not_8_out, in[5]);
  not not_9 (not_9_out, in[5]);
  not not_10 (not_10_out, in[6]);
  not not_11 (not_11_out, in[6]);
  and and_1 (and_1_out, in[5], not_10_out);
  and and_2 (and_2_out, in[2], not_5_out, not_8_out);
  and and_3 (and_3_out, in[3], not_5_out, not_8_out, not_10_out);
  and and_4 (and_4_out, in[1], not_3_out, not_5_out, not_10_out);
  and and_5 (and_5_out, in[3], not_5_out, not_8_out, not_10_out);
  and and_6 (and_6_out, in[5], not_10_out);
  and and_7 (and_7_out, not_1_out, not_2_out, not_4_out, not_6_out, not_7_out, not_9_out, in[6]);
  and and_8 (and_8_out, not_1_out, not_2_out, not_4_out, not_6_out, not_7_out, not_9_out, not_11_out, in[7]);
  and and_9 (and_9_out, not_1_out, not_2_out, not_4_out, not_6_out, not_7_out, in[5]);
  and and_10 (and_10_out, not_1_out, not_2_out, not_4_out, not_6_out, in[4]);
  and and_11 (and_11_out, not_1_out, not_2_out, not_4_out, not_6_out, not_7_out, not_9_out, in[6]);
  and and_12 (and_12_out, not_1_out, not_2_out, not_4_out, not_6_out, not_7_out, not_9_out, not_11_out, in[7]);
  and and_13 (and_13_out, not_1_out, not_2_out, not_4_out, in[3]);
  and and_14 (and_14_out, not_1_out, not_2_out, in[2]);
  and and_15 (and_15_out, not_1_out, not_2_out, not_4_out, not_6_out, not_7_out, not_9_out, not_11_out, in[7]);
  and and_16 (and_16_out, not_1_out, not_2_out, not_4_out, not_6_out, not_7_out, in[5]);
  and and_17 (and_17_out, not_1_out, not_2_out, not_4_out, in[3]);
  and and_18 (and_18_out, not_1_out, in[1]);
  or or_1 (or_3_out[2], in[4], and_1_out, in[6], in[7]);
  or or_2 (or_3_out[1], and_2_out, and_3_out, in[6], in[7]);
  or or_3 (or_3_out[0], and_4_out, and_5_out, and_6_out, in[7]);
  or or_4 (or_4_out[2], and_7_out, and_8_out, and_9_out, and_10_out);
  or or_5 (or_4_out[1], and_11_out, and_12_out, and_13_out, and_14_out);
  or or_6 (or_4_out[0], and_15_out, and_16_out, and_17_out, and_18_out);
  Add #(.Bits(3)) add_1 (.a(or_3_out), .b(or_4_out), .c_i(1'b0), .s(out[2:0]), .c_o(out[3]));
endmodule
